# Fritzing sketch link-pedal2key-2 (saved by Fritzing 0.9.3b)

parts:
  Arduino_Micro = Arduino Micro (Rev3)
  Joystick = Thumb Joystick
  Audio_Jack = 2.5mm Audio Jack [package=stereojack2.5mm_stereojack2.5mm]

nets:
  GND: Arduino_Micro.GND, Joystick.GND, Audio_Jack.RIGHT
  N1: Arduino_Micro.D4_PWM/A6, Audio_Jack.LEFT
  N2: Arduino_Micro.D7, Joystick.VCC
  N3: Arduino_Micro.5V, Joystick.SEL
  N4: Arduino_Micro.A3, Joystick.VERT
  N5: Arduino_Micro.A0, Joystick.HORZ
