# Fritzing sketch link-pedal2key (saved by Fritzing 0.9.3b)

parts:
  Arduino_Micro = Arduino Micro (Rev3)
  Joystick = Thumb Joystick
  Audio_Jack = 2.5mm Audio Jack [package=stereojack2.5mm_stereojack2.5mm]

nets:
  GND: Arduino_Micro.GND, Joystick.GND, Audio_Jack.RIGHT
  N1: Arduino_Micro.D2/SDA, Joystick.VCC
  N2: Arduino_Micro.D7, Audio_Jack.LEFT
  N3: Arduino_Micro.5V, Joystick.SEL
  N4: Arduino_Micro.A1, Joystick.VERT
  N5: Arduino_Micro.A0, Joystick.HORZ
