# Fritzing sketch ultrasonic-distance-measurement (saved by Fritzing 0.9.3b)
breadboards: 1

parts:
  パーツ1 = Arduino Uno (Rev3)
  HC-SR04 = hc-sr04

nets:
  N1: パーツ1.D8, HC-SR04.Trig
  N2: パーツ1.D9_PWM, HC-SR04.Echo
  N3: パーツ1.D10_PWM/SS, HC-SR04.VCC
  N4: パーツ1.D11_PWM/MOSI, HC-SR04.GND
