# Fritzing sketch wifi_esp-wroom-02_v3.3 (saved by Fritzing 0.9.3b)
breadboards: 1

parts:
  パーツ1 = Arduino Uno (Rev3)
  R1 = Resistor [tolerance=±5% resistance=10k package=THT]
  R2 = Resistor [tolerance=±5% resistance=10k package=THT]
  part = Resistor [tolerance=±5% resistance=10k package=THT]
  W1 = ESP-WROOM2-02 simple breakout [package="DIP (Dual Inline) [THT]"]

nets:
  N1: パーツ1.D2, W1.TX0
  N2: パーツ1.D3_PWM, W1.RX0
  3V3: パーツ1.3V3, R1.Pin_0, R2.Pin_0, part.Pin_0, W1.3V3
  GND: パーツ1.GND, W1.GND
  N3: R1.Pin_1, W1.RST
  N4: R2.Pin_1, W1.EN
  N5: part.Pin_1, W1.IO0

notes:
  Arduinoから3.3vで出力
