# Fritzing sketch wifi_esp-wroom-02_v5-1 (saved by Fritzing 0.9.3b)
breadboards: 1

parts:
  パーツ1 = Arduino Uno (Rev3)
  R1 = Resistor [tolerance=±5% resistance=10k package=THT]
  R2 = Resistor [tolerance=±5% resistance=10k package=THT]
  part = Resistor [tolerance=±5% resistance=10k package=THT]
  W1 = ESP-WROOM2-02 simple breakout [package="DIP (Dual Inline) [THT]"]
  U1 = Voltage Regulator - 3.3V [package="TO220 [THT]"]
  C1 = Electrolytic Capacitor [capacitance=1µF package="100 mil [THT, electrolytic]"]
  C2 = Ceramic Capacitor [capacitance=100nF package="100 mil [THT, multilayer]"]

nets:
  N1: パーツ1.D2, W1.TX0
  N2: パーツ1.D3_PWM, W1.RX0
  N3: パーツ1.5V, U1.input_voltage, C2.0
  GND: パーツ1.GND, W1.GND, U1.GND, C1.+, C2.1
  N4: R1.Pin_0, R2.Pin_0, part.Pin_0, W1.3V3, U1.output_voltage, C1.-
  N5: R1.Pin_1, W1.RST
  N6: R2.Pin_1, W1.EN
  N7: part.Pin_1, W1.IO0
